# Fritzing sketch CW_Beacon (saved by Fritzing 0.9.3b)
perfboards: 1

parts:
  Mod1 = Raspberry Pi Pico
  LED1 = smd LED [color="Yellow (595nm)" package="0603 [SMD]"]  # not connected
  LED2 = smd LED [color="Green (570nm)" package="0603 [SMD]"]  # not connected
  LED3 = smd LED [color="Red (633nm)" package="0603 [SMD]"]  # not connected
  S1 = Reed switch [part_number=D1A050000 package=THT]  # not connected
  Q2 = NPN-Transistor [package="SOT-23 [SMD]"]  # not connected
  R1 = Resistor [tolerance=±5% resistance=220 package="0402 [SMD]"]
  R2 = Resistor [tolerance=±5% resistance=220 package="2010 [SMD]"]
  R3 = Resistor [tolerance=±5% resistance=220 package="2512 [SMD]"]
  R4 = Resistor [tolerance=±5% resistance=220 package="0402 [SMD]"]
  Q1 = PNP-Transistor [package="SOT-23 [SMD]"]
  SG1 = Buzzer 12mm [package=buzzer-12mm-ns]
  U2 = LIPO-110mAh [package=lipo-110]  # not connected
  U2_2 = LIPO-110mAh [package=lipo-110]
  R5 = Resistor [tolerance=±5% resistance=220 package="0402 [SMD]"]

nets:
  N1: Mod1.pin_4, R5.Pin_1
  N2: Mod1.pin_20, R4.Pin_1
  N3: Mod1.pin_29, R3.Pin_1
  N4: Mod1.pin_31, R2.Pin_1
  N5: Mod1.pin_32, R1.Pin_1
  N6: Mod1.pin_33, Mod1.pin_38, Mod1.pin_42, Q1.1, SG1.2, U2_2.-
  N7: R4.Pin_0, Q1.0

custom parts:
  Raspberry Pi Pico: Raspberry Pi Pico. Based around the RP2040 microcontroller the Pico is a low cost microcontroller device bringing Raspberry Pi quality, cost, and easy of use to the microcontroller space. Jan 2021, Split part in to two versions: tht (this one) and SMD. This one will drill holes for a .1 in header in pcb to allow plugging in the module as well as providing pads to solder the module to the top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
