# Fritzing sketch CW_Beacon2 (saved by Fritzing 0.9.3b)
perfboards: 1

parts:
  Mod2 = Raspberry Pi Pico
  R7 = Resistor [tolerance=±5% resistance=220 package="0402 [SMD]"]
  R9 = Resistor [tolerance=±5% resistance=220 package="0402 [SMD]"]  # not connected
  R10 = Resistor [tolerance=±5% resistance=220 package="0402 [SMD]"]  # not connected
  R6 = Resistor [tolerance=±5% resistance=220 package="0402 [SMD]"]
  Q3 = NPN-Transistor [part_number=S5080 package="SOT-23 [SMD]"]
  R11 = TRIMPOT [package=3386u]
  J1 = Piezo Speaker
  R12 = Resistor [tolerance=±5% resistance=220 package="0402 [SMD]"]
  R13 = Resistor [tolerance=±5% resistance=220 package="0402 [SMD]"]
  LED1 = LED - 5mm [color="Red (633nm)" package="5 mm [THT]"]
  LED2 = LED - 5mm [color="Blue (505nm)" package="5 mm [THT]"]
  LED3 = LED - 5mm [color="Green (555nm)" package="5 mm [THT]"]
  Q4 = PNP-Transistor [package="TO92 [THT]"]
  R14 = Resistor [tolerance=±5% resistance=220 package=THT]
  DIP-Relay1 = DIP-Relay-D31A [part_number="Reed Relay"]

nets:
  N1: Mod2.pin_3, Mod2.pin_8, Mod2.pin_13, Mod2.pin_18, Mod2.pin_23, Mod2.pin_28, Mod2.pin_33, Mod2.pin_38, Mod2.pin_42, Q3.2, LED1.cathode, LED2.cathode, LED3.cathode, DIP-Relay1.COIL1_+
  N2: Mod2.pin_20, Q4.E, R14.Pin_0, DIP-Relay1.Coil2_-
  N3: Mod2.pin_29, R12.Pin_0
  N4: Mod2.pin_31, R13.Pin_0
  N5: Mod2.pin_32, R7.Pin_0
  N6: Mod2.pin_39, J1.pin2, Q4.C
  N7: R7.Pin_1, LED2.anode
  N8: R6.Pin_0, Q3.0
  N9: Q3.1, R11.CW
  N10: R11.WIPER, J1.pin1
  N11: R12.Pin_1, LED3.anode
  N12: R13.Pin_1, LED1.anode
  N13: Q4.B, R14.Pin_1

custom parts:
  Raspberry Pi Pico: Raspberry Pi Pico. Based around the RP2040 microcontroller the Pico is a low cost microcontroller device bringing Raspberry Pi quality, cost, and easy of use to the microcontroller space. Jan 2021, Split part in to two versions: tht (this one) and SMD. This one will drill holes for a .1 in header in pcb to allow plugging in the module as well as providing pads to solder the module to the top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
